# Fritzing sketch MPU6050 Fritzing (saved by Fritzing 0.9.6b)
breadboards: 1

parts:
  Part1 = InvenSense MPU6050
  Mod1 = Raspberry Pi Pico

nets:
  N1: Part1.VCC, Mod1.pin_35
  N2: Part1.GND, Mod1.pin_3, Mod1.pin_8, Mod1.pin_13, Mod1.pin_18, Mod1.pin_23, Mod1.pin_28, Mod1.pin_33, Mod1.pin_38
  N3: Part1.SCL, Mod1.pin_2
  N4: Part1.SDA, Mod1.pin_1

custom parts:
  Raspberry Pi Pico: Raspberry Pi Pico. Based around the RP2040 microcontroller the Pico is a low cost microcontroller device bringing Raspberry Pi quality, cost, and easy of use to the microcontroller space. Jan 2021, Split part in to two versions: SMD (this one) and tht. This one is single sided and uses the castellation pads to solder the module to the board (no holes, other than for the USB connector!). The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
